# Fritzing sketch Captus (saved by Fritzing 0.9.3b)

parts:
  Mustache_Motor = Basic Servo
  Food_Motor = Basic Servo
  Greeting_Motor = Basic Servo
  CenterFood_Sensor = PHOTOCELL [package=photocell]
  R8 = Resistor [tolerance=±5% resistance=220 package=THT]
  Rigth_Eye = RGB LED (com. cathode, rgb) [package="5 mm [THT]"]
  R12 = Resistor [tolerance=±5% resistance=120 package=THT]
  R13 = Resistor [tolerance=±5% resistance=120 package=THT]
  R14 = Resistor [tolerance=±5% resistance=120 package=THT]
  R2 = Resistor [tolerance=±5% resistance=120 package=THT]
  Left_Eye = RGB LED (com. cathode, rgb) [package="5 mm [THT]"]
  R15 = Resistor [tolerance=±5% resistance=120 package=THT]
  R16 = Resistor [tolerance=±5% resistance=120 package=THT]
  Left_Speaker = Loudspeaker
  Arduino_Head = Arduino Uno (Rev3)
  Left_Sonar = HC-SR04 Ultrasonic Rangemeter
  Center_Sonar = HC-SR04 Ultrasonic Rangemeter
  Right_Sonar = HC-SR04 Ultrasonic Rangemeter
  Elbrows_Motor = Basic Servo
  DFRobot_DFPlayer = DFRobot DFPlayer Mini [part_number=DFR0299]
  R17 = Resistor [tolerance=±5% resistance=120 package=THT]
  VCC_MOTORS = Battery block 9V
  U2 = Voltage Regulator [package=to220-adj]
  R18 = Resistor [tolerance=±5% resistance=720 package=THT]
  R19 = Resistor [tolerance=±5% resistance=240 package=THT]
  Body_Motor = Basic Servo
  VCC_LOGIC = 4 x AAA Battery Mount
  Arduino_Body = Arduino Uno (Rev3)

nets:
  GND: Mustache_Motor.gnd, Food_Motor.gnd, Greeting_Motor.gnd, R8.Pin_1, Rigth_Eye.common_cathode, Left_Eye.common_cathode, Arduino_Head.GND, Left_Sonar.GND, Center_Sonar.GND, Right_Sonar.GND, Elbrows_Motor.gnd, DFRobot_DFPlayer.GND-1, DFRobot_DFPlayer.GND-2, VCC_MOTORS.-, R18.Pin_0, Body_Motor.gnd, VCC_LOGIC.-, Arduino_Body.GND
  VCC: Mustache_Motor.vcc, Food_Motor.vcc, Greeting_Motor.vcc, Elbrows_Motor.vcc, U2.OUT, R19.Pin_1, Body_Motor.vcc
  N1: Food_Motor.pulse, Arduino_Head.D7
  N2: Greeting_Motor.pulse, Arduino_Head.D6_PWM
  5V: CenterFood_Sensor.P$1, Arduino_Head.5V, DFRobot_DFPlayer.VCC
  N3: CenterFood_Sensor.P$2, R8.Pin_0, Arduino_Head.A0
  N4: Rigth_Eye.red_anode, R13.Pin_0
  N5: Rigth_Eye.green_anode, R14.Pin_0
  N6: Rigth_Eye.blue_anode, R12.Pin_0
  N7: R12.Pin_1, R16.Pin_1, Arduino_Head.D11_PWM/MOSI
  N8: R13.Pin_1, R15.Pin_1, Arduino_Head.D9_PWM
  N9: R14.Pin_1, R2.Pin_1, Arduino_Head.D10_PWM/SS
  N10: R2.Pin_0, Left_Eye.green_anode
  N11: Left_Eye.red_anode, R15.Pin_0
  N12: Left_Eye.blue_anode, R16.Pin_0
  N13: Left_Speaker.pin1, DFRobot_DFPlayer.SPK_2
  N14: Left_Speaker.pin2, DFRobot_DFPlayer.SPK_1
  N15: Arduino_Head.D12/MISO, R17.Pin_0
  N16: Arduino_Head.D13/SCK, DFRobot_DFPlayer.TX
  N17: Arduino_Head.D2, Arduino_Body.D2
  N18: Arduino_Head.D5_PWM, Elbrows_Motor.pulse
  VCC_LOGIC: Arduino_Head.VIN, VCC_LOGIC.+, Arduino_Body.VIN
  VCC_2: Left_Sonar.VCC, Center_Sonar.VCC, Right_Sonar.VCC, Arduino_Body.5V
  N19: Left_Sonar.Trig, Arduino_Body.D8
  N20: Left_Sonar.Echo, Arduino_Body.D7
  N21: Center_Sonar.Trig, Arduino_Body.D10_PWM/SS
  N22: Center_Sonar.Echo, Arduino_Body.D9_PWM
  N23: Right_Sonar.Trig, Arduino_Body.D12/MISO
  N24: Right_Sonar.Echo, Arduino_Body.D11_PWM/MOSI
  N25: DFRobot_DFPlayer.RX, R17.Pin_1
  N26: VCC_MOTORS.+, U2.IN
  N27: U2.ADJ, R18.Pin_1, R19.Pin_0
  N28: Body_Motor.pulse, Arduino_Body.D6_PWM
