# Fritzing sketch Captus (saved by Fritzing 0.9.3b)

parts:
  Mustache_Motor = Basic Servo
  Food_Motor = Basic Servo
  Greeting_Motor = Basic Servo
  Arduino_Slave = Arduino Uno (Rev3)
  VCC1 = 4 x AAA Battery Mount
  RightFood_Sensor = PHOTOCELL [package=photocell]
  LeftFood_Sensor = PHOTOCELL [package=photocell]
  CenterFood_Sensor = PHOTOCELL [package=photocell]
  R7 = Resistor [tolerance=±5% resistance=220 package=THT]
  R8 = Resistor [tolerance=±5% resistance=220 package=THT]
  R9 = Resistor [tolerance=±5% resistance=220 package=THT]
  Rigth_Eye = RGB LED (com. cathode, rgb) [package="5 mm [THT]"]
  R12 = Resistor [tolerance=±5% resistance=120 package=THT]
  R13 = Resistor [tolerance=±5% resistance=120 package=THT]
  R14 = Resistor [tolerance=±5% resistance=120 package=THT]
  R2 = Resistor [tolerance=±5% resistance=120 package=THT]
  Left_Eye = RGB LED (com. cathode, rgb) [package="5 mm [THT]"]
  R15 = Resistor [tolerance=±5% resistance=120 package=THT]
  R16 = Resistor [tolerance=±5% resistance=120 package=THT]
  Arduino_Music = LilyPad Arduino Simple Board
  Body_Motor = Basic Servo
  Left_Speaker = Loudspeaker
  Right_Speaker = Loudspeaker
  Arduino_Master = Arduino Uno (Rev3)
  Left_Sonar = HC-SR04 Ultrasonic Rangemeter
  Center_Sonar = HC-SR04 Ultrasonic Rangemeter
  Right_Sonar = HC-SR04 Ultrasonic Rangemeter

nets:
  GND: Mustache_Motor.gnd, Food_Motor.gnd, Greeting_Motor.gnd, Arduino_Slave.GND, VCC1.-, R7.Pin_1, R8.Pin_1, R9.Pin_1, Rigth_Eye.common_cathode, Left_Eye.common_cathode, Arduino_Music.GND, Body_Motor.gnd, Left_Speaker.pin2, Right_Speaker.pin2, Arduino_Master.GND, Left_Sonar.GND, Center_Sonar.GND, Right_Sonar.GND
  VCC: Mustache_Motor.vcc, Food_Motor.vcc, Greeting_Motor.vcc, VCC1.+, Body_Motor.vcc
  N1: Mustache_Motor.pulse, Arduino_Master.D8
  N2: Food_Motor.pulse, Arduino_Master.D7
  N3: Greeting_Motor.pulse, Arduino_Master.D6_PWM
  N4: Arduino_Slave.A4/SDA, Arduino_Music.A4, Arduino_Master.A4/SDA
  N5: Arduino_Slave.A5/SCL, Arduino_Music.A5, Arduino_Master.A5/SCL
  N6: Arduino_Slave.D8, Left_Sonar.Trig
  N7: Arduino_Slave.D9_PWM, Center_Sonar.Echo
  N8: Arduino_Slave.D10_PWM/SS, Center_Sonar.Trig
  N9: Arduino_Slave.D11_PWM/MOSI, Right_Sonar.Echo
  N10: Arduino_Slave.D12/MISO, Right_Sonar.Trig
  N11: Arduino_Slave.D6_PWM, Body_Motor.pulse
  N12: Arduino_Slave.D7, Left_Sonar.Echo
  5V: Arduino_Slave.5V, RightFood_Sensor.P$1, LeftFood_Sensor.P$1, CenterFood_Sensor.P$1, Arduino_Music.VCC, Arduino_Master.5V, Left_Sonar.VCC, Center_Sonar.VCC, Right_Sonar.VCC
  N13: RightFood_Sensor.P$2, R7.Pin_0, Arduino_Master.A2
  N14: LeftFood_Sensor.P$2, R9.Pin_0, Arduino_Master.A0
  N15: CenterFood_Sensor.P$2, R8.Pin_0, Arduino_Master.A1
  N16: Rigth_Eye.red_anode, R13.Pin_0
  N17: Rigth_Eye.green_anode, R14.Pin_0
  N18: Rigth_Eye.blue_anode, R12.Pin_0
  N19: R12.Pin_1, R16.Pin_1, Arduino_Master.D11_PWM/MOSI
  N20: R13.Pin_1, R15.Pin_1, Arduino_Master.D9_PWM
  N21: R14.Pin_1, R2.Pin_1, Arduino_Master.D10_PWM/SS
  N22: R2.Pin_0, Left_Eye.green_anode
  N23: Left_Eye.red_anode, R15.Pin_0
  N24: Left_Eye.blue_anode, R16.Pin_0
  N25: Arduino_Music.A2, Left_Speaker.pin1, Right_Speaker.pin1
